# Fritzing sketch parking sensor (saved by Fritzing 0.9.3b)
breadboards: 1

parts:
  Parça1 = Arduino Uno (Rev3)
  hc-sr1 = hc-sr04
  LED1 = LEDs [package=led10mm]
  LED2 = LEDs [package=led10mm]
  LED3 = LEDs [package=led10mm]
  LED4 = LEDs [package=led10mm]
  J1 = Piezo Speaker
  R1 = Resistor [tolerance=±5% resistance=220 package="0402 [SMD]"]

nets:
  N1: Parça1.D8, LED4.A
  N2: Parça1.D9_PWM, LED3.A
  N3: Parça1.D10_PWM/SS, LED2.A
  N4: Parça1.D11_PWM/MOSI, LED1.A
  N5: Parça1.D5_PWM, J1.pin2
  N6: Parça1.D6_PWM, hc-sr1.Echo
  N7: Parça1.D7, hc-sr1.Trig
  5V: Parça1.5V, hc-sr1.VCC
  GND: Parça1.GND, hc-sr1.GND, J1.pin1, R1.Pin_1
  N8: LED1.C, LED2.C, LED3.C, LED4.C, R1.Pin_0
